# Fritzing sketch MasterSlave Board (saved by Fritzing 0.9.3b)

parts:
  Part1 = Arduino Uno (Rev3)
  Part2 = Arduino Uno (Rev3)
  R1 = Rotary Potentiometer (Small) [maximum_resistance=100kΩ package=THT]
  LED1 = LED - 5mm [color="Red (633nm)" package="5 mm [THT]"]

nets:
  N1: Part1.A4/SDA, Part2.A4/SDA
  N2: Part1.A5/SCL, Part2.A5/SCL
  N3: Part1.D13/SCK, LED1.anode
  GND: Part1.GND, Part2.GND, R1.leg2, LED1.cathode
  VIN: Part1.VIN, Part2.5V
  N4: Part2.A0, R1.wiper
  N5: Part2.3V3, R1.leg1
